// Logisim project d8_new.circ as structural Verilog
module pipeline (
  input  CLK,
  input  [7:0] D,
  input  LOAD_M,
  input  [3:0] FLAGS,
  output [1:0] CYCLE,
  output SKIP,
  output [15:0] CTRL0,
  output [15:0] CTRL1,
  output [15:0] CTRL2,
  output [15:0] CTRL3
);

  wire ic_xx02_1_y1, ic_xx02_1_y2, ic_xx02_1_y4, transistor_1_out;
  wire [3:3] ic_xx163_1_q;
  wire [7:0] ic_xx174_1_q0;
  wire [7:4] ic_xx574_2_o, ic_xx574_4_o, ic_xx574_5_o, ic_xx574_7_o, ic_xx574_8_o, ic_xx574_10_o,
       ic_xx574_11_o, undriven;

  Transistor #(.\type ("n")) transistor_1 (.in(1'b0), .out(transistor_1_out), .gate(SKIP));
  Pull_Resistor #(.pull(1)) pull_resistor_1 (.node(transistor_1_out));
  IC_xx163 ic_xx163_1 (
    .CLR_L(transistor_1_out), .CLK(CLK), .ENP(1'b1), .Q({ic_xx163_1_q[3], SKIP, CYCLE}), .ENT(1'b1),
    .LOAD_L(1'b1));  // open: D, RCO
  IC_xx02 ic_xx02_1 (
    .Y1(ic_xx02_1_y1), .A1(ic_xx02_1_y2), .B1(ic_xx02_1_y2), .Y2(ic_xx02_1_y2), .A2(CYCLE[0]), .B2(CYCLE[1]),
    .Y4(ic_xx02_1_y4), .B4(ic_xx02_1_y1), .A4(SKIP));  // open: Y3, B3, A3
  IC_xx574 ic_xx574_1 (.OE_L(1'b0), .D(D), .O(CTRL0[7:0]), .CP(SKIP));
  IC_xx174 ic_xx174_1 (
    .MR(ic_xx02_1_y4), .D0(D[0]), .D1(D[1]), .D2(D[2]), .D3(D[3]), .Q0(ic_xx174_1_q0[0]),
    .Q1(ic_xx174_1_q0[1]), .Q2(ic_xx174_1_q0[2]), .Q3(ic_xx174_1_q0[3]), .CP(LOAD_M));  // open: D4, D5, Q4, Q5
  IC_xx574 ic_xx574_2 (.OE_L(1'b0), .D({undriven, FLAGS}), .O({ic_xx574_2_o, CTRL0[15:12]}), .CP(SKIP));
  IC_xx574 ic_xx574_3 (.OE_L(1'b0), .D(CTRL0[7:0]), .O(CTRL1[7:0]), .CP(SKIP));
  IC_xx574 ic_xx574_4 (.OE_L(1'b0), .D(ic_xx174_1_q0), .O({ic_xx574_4_o, CTRL1[11:8]}), .CP(SKIP));
  IC_xx574 ic_xx574_5 (.OE_L(1'b0), .D({ic_xx574_2_o, CTRL0[15:12]}), .O({ic_xx574_5_o, CTRL1[15:12]}), .CP(SKIP));
  IC_xx574 ic_xx574_6 (.OE_L(1'b0), .D(CTRL1[7:0]), .O(CTRL2[7:0]), .CP(SKIP));
  IC_xx574 ic_xx574_7 (.OE_L(1'b0), .D({ic_xx574_4_o, CTRL1[11:8]}), .O({ic_xx574_7_o, CTRL2[11:8]}), .CP(SKIP));
  IC_xx574 ic_xx574_8 (.OE_L(1'b0), .D({ic_xx574_5_o, CTRL1[15:12]}), .O({ic_xx574_8_o, CTRL2[15:12]}), .CP(SKIP));
  IC_xx574 ic_xx574_9 (.OE_L(1'b0), .D(CTRL2[7:0]), .O(CTRL3[7:0]), .CP(SKIP));
  IC_xx574 ic_xx574_10 (.OE_L(1'b0), .D({ic_xx574_7_o, CTRL2[11:8]}), .O({ic_xx574_10_o, CTRL3[11:8]}), .CP(SKIP));
  IC_xx574 ic_xx574_11 (.OE_L(1'b0), .D({ic_xx574_8_o, CTRL2[15:12]}), .O({ic_xx574_11_o, CTRL3[15:12]}), .CP(SKIP));
  // LedBar #(.inputtype("row"), .matrixcols(16)) ledbar_1: pin names not known; wires that end beside it: {CTRL0[15:12], 4'b0000, CTRL0[7:0]}
  // LedBar #(.inputtype("row"), .matrixcols(16)) ledbar_2: pin names not known; wires that end beside it: CTRL1
  // LedBar #(.inputtype("row"), .matrixcols(16)) ledbar_3: pin names not known; wires that end beside it: CTRL2
  // LedBar #(.inputtype("row"), .matrixcols(16)) ledbar_4: pin names not known; wires that end beside it: CTRL3

  assign CTRL0[11:8] = 4'b0000;
endmodule

// xx02
module DIP_xx02 (
  input  Vcc,
  input  A1,
  input  B1,
  input  B4,
  input  A4,
  input  A2,
  input  B2,
  input  B3,
  input  GND,
  input  A3,
  output Y1,
  output Y4,
  output Y2,
  output Y3
);

  nor nor_1 (Y1, A1, B1);
  nor nor_2 (Y2, A2, B2);
  nor nor_3 (Y4, A4, B4);
  nor nor_4 (Y3, A3, B3);

  // Notes on the sheet:
  //   A4: pull=up
  //   B3: pull=up
  //   Vcc: pull=up
  //   B4: pull=up
  //   A2: pull=up
  //   A1: pull=up
  //   B1: pull=up
endmodule

// xx163
module DIP_xx163 (
  input  CLR_L,
  input  Vcc,
  input  CLK,
  input  A,
  input  B,
  input  C,
  input  D,
  input  ENP,
  input  ENT,
  input  GND,
  input  LOAD_L,
  output RCO,
  output Q_A,
  output Q_B,
  output Q_C,
  output Q_D
);

  _74163 u_74163_1 (
    .pin1(CLR_L), .pin2(CLK), .pin3(A), .pin4(B), .pin5(C), .pin6(D), .pin7(ENP), .pin15(RCO), .pin14(Q_A),
    .pin13(Q_B), .pin12(Q_C), .pin11(Q_D), .pin10(ENT), .pin9(LOAD_L));
endmodule

// xx174
module DIP_xx174 (
  input  MR,
  input  Vcc,
  input  D0,
  input  D5,
  input  D1,
  input  D4,
  input  D2,
  input  D3,
  input  GND,
  input  CP,
  output Q0,
  output Q5,
  output Q1,
  output Q4,
  output Q2,
  output Q3
);

  D_Flip_Flop d_ff_1 (.clk(CP), .D(D0), .Q(Q0), .preset(1'b0), .reset(MR));  // open: Qn
  D_Flip_Flop d_ff_2 (.clk(CP), .D(D1), .Q(Q1), .preset(1'b0), .reset(MR));  // open: Qn
  D_Flip_Flop d_ff_3 (.clk(CP), .D(D2), .Q(Q2), .preset(1'b0), .reset(MR));  // open: Qn
  D_Flip_Flop d_ff_4 (.clk(CP), .D(D5), .Q(Q5), .preset(1'b0), .reset(MR));  // open: Qn
  D_Flip_Flop d_ff_5 (.clk(CP), .D(D4), .Q(Q4), .preset(1'b0), .reset(MR));  // open: Qn
  D_Flip_Flop d_ff_6 (.clk(CP), .D(D3), .Q(Q3), .preset(1'b0), .reset(MR));  // open: Qn
endmodule

// xx540
module DIP_xx540 (
  input  OE1_L,
  input  Vcc,
  input  D0,
  input  OE2_L,
  input  D1,
  input  D2,
  input  D3,
  input  D4,
  input  D5,
  input  D6,
  input  D7,
  input  GND,
  output Q0,
  output Q1,
  output Q2,
  output Q3,
  output Q4,
  output Q5,
  output Q6,
  output Q7
);

  wire and_1_out, not_1_out, not_2_out;

  not not_1 (not_1_out, OE1_L);
  and and_1 (and_1_out, not_1_out, not_2_out);
  not not_2 (not_2_out, OE2_L);
  assign Q0 = and_1_out ? D0 : 1'bz;  // Controlled_Buffer controlled_buffer_1
  assign Q1 = and_1_out ? D1 : 1'bz;  // Controlled_Buffer controlled_buffer_2
  assign Q2 = and_1_out ? D2 : 1'bz;  // Controlled_Buffer controlled_buffer_3
  assign Q3 = and_1_out ? D3 : 1'bz;  // Controlled_Buffer controlled_buffer_4
  assign Q4 = and_1_out ? D4 : 1'bz;  // Controlled_Buffer controlled_buffer_5
  assign Q5 = and_1_out ? D5 : 1'bz;  // Controlled_Buffer controlled_buffer_6
  assign Q6 = and_1_out ? D6 : 1'bz;  // Controlled_Buffer controlled_buffer_7
  assign Q7 = and_1_out ? D7 : 1'bz;  // Controlled_Buffer controlled_buffer_8

  // Notes on the sheet:
  //   D2: pull=up
  //   D3: pull=up
  //   D4: pull=up
  //   D5: pull=up
  //   D6: pull=up
  //   D7: pull=up
  //   OE1_L: pull=up
  //   D0: pull=up
  //   D1: pull=up
  //   OE2_L: pull=up
endmodule

// xx574
module DIP_xx574 (
  input  OE_L,
  input  Vcc,
  input  D0,
  input  D1,
  input  D2,
  input  D3,
  input  D4,
  input  D5,
  input  D6,
  input  D7,
  input  GND,
  input  CP,
  output Q0,
  output Q1,
  output Q2,
  output Q3,
  output Q4,
  output Q5,
  output Q6,
  output Q7
);

  wire not_1_out;
  wire [7:0] register_1_q;

  not not_1 (not_1_out, OE_L);
  Register register_1 (.D({D7, D6, D5, D4, D3, D2, D1, D0}), .en(1'b1), .Q(register_1_q), .clk(CP), .clr(1'b0));
  assign {Q7, Q6, Q5, Q4, Q3, Q2, Q1, Q0} = not_1_out ? register_1_q : 8'bz;  // Controlled_Buffer controlled_buffer_1

  // Notes on the sheet:
  //   D1: pull=up
  //   D2: pull=up
  //   D3: pull=up
  //   D4: pull=up
  //   D5: pull=up
  //   D6: pull=up
  //   D7: pull=up
  //   OE_L: pull=up
  //   D0: pull=up
  //   CP: pull=up
endmodule

module IC_xx02 (
  input  A1,
  input  B4,
  input  B1,
  input  A4,
  input  A2,
  input  B3,
  input  B2,
  input  A3,
  output Y1,
  output Y4,
  output Y2,
  output Y3
);

  DIP_xx02 dip_xx02_1 (
    .Y1(Y1), .A1(A1), .B1(B1), .Y2(Y2), .A2(A2), .B2(B2), .Y4(Y4), .B4(B4), .A4(A4), .Y3(Y3), .B3(B3), .A3(A3));  // open: GND, Vcc

  // Notes on the sheet:
  //   A1: pull=up
  //   B1: pull=up
  //   A2: pull=up
  //   B4: pull=up
  //   A4: pull=up
  //   B3: pull=up
endmodule

module IC_xx163 (
  input  CLR_L,
  input  CLK,
  input  [3:0] D,
  input  ENP,
  input  ENT,
  input  LOAD_L,
  output RCO,
  output [3:0] Q
);

  DIP_xx163 dip_xx163_1 (
    .CLR_L(CLR_L), .CLK(CLK), .A(D[0]), .B(D[1]), .C(D[2]), .D(D[3]), .ENP(ENP), .RCO(RCO), .Q_A(Q[0]),
    .Q_B(Q[1]), .Q_C(Q[2]), .Q_D(Q[3]), .ENT(ENT), .LOAD_L(LOAD_L));  // open: GND, Vcc
endmodule

module IC_xx174 (
  input  MR,
  input  D0,
  input  D1,
  input  D2,
  input  D3,
  input  D4,
  input  D5,
  input  CP,
  output Q0,
  output Q1,
  output Q2,
  output Q3,
  output Q4,
  output Q5
);

  DIP_xx174 dip_xx174_1 (
    .MR(MR), .Q0(Q0), .D0(D0), .D1(D1), .Q1(Q1), .D2(D2), .Q2(Q2), .Q5(Q5), .D5(D5), .D4(D4), .Q4(Q4),
    .D3(D3), .Q3(Q3), .CP(CP));  // open: GND, Vcc
endmodule

module IC_xx540 (
  input  OE1_L,
  input  OE2_L,
  input  [7:0] D,
  output [7:0] Q
);

  DIP_xx540 dip_xx540_1 (
    .OE1_L(OE1_L), .D0(D[0]), .D1(D[1]), .D2(D[2]), .D3(D[3]), .D4(D[4]), .D5(D[5]), .D6(D[6]), .D7(D[7]),
    .OE2_L(OE2_L), .Q0(Q[0]), .Q1(Q[1]), .Q2(Q[2]), .Q3(Q[3]), .Q4(Q[4]), .Q5(Q[5]), .Q6(Q[6]), .Q7(Q[7]));  // open: GND, Vcc
endmodule

module IC_xx574 (
  input  OE_L,
  input  [7:0] D,
  input  CP,
  output [7:0] O
);

  DIP_xx574 dip_xx574_1 (
    .OE_L(OE_L), .D0(D[0]), .D1(D[1]), .D2(D[2]), .D3(D[3]), .D4(D[4]), .D5(D[5]), .D6(D[6]), .D7(D[7]),
    .Q0(O[0]), .Q1(O[1]), .Q2(O[2]), .Q3(O[3]), .Q4(O[4]), .Q5(O[5]), .Q6(O[6]), .Q7(O[7]), .CP(CP));  // open: GND, Vcc

  // Notes on the sheet:
  //   OE_L: pull=up
  //   D: pull=up
  //   CP: pull=up
endmodule
